# Fritzing sketch sketch (saved by Fritzing 0.9.2b)
breadboards: 1

parts:
  U1 = attiny85 [package=dip]
  Part1 = FTDI Basic Programmer
  D1 = Diode [package=diode-hv]
  R1 = Resistor [tolerance=±5% resistance=330 package="2010 [SMD]"]
  Q1 = NPN-Transistor [package="TO92 [THT]"]

nets:
  N1: U1.Pin_2, D1.A, Q1.E
  N2: U1.Pin_4, Part1.GND
  N3: U1.Pin_8, Part1.POWER
  N4: Part1.RXI, Q1.C
  N5: Part1.TXO, D1.C, R1.Pin_1
  N6: R1.Pin_0, Q1.B
